# Fritzing sketch LightPatterns (saved by Fritzing 0.9.4)
breadboards: 1

parts:
  Part1 = Adafruit HUZZAH32 ESP32 Feather [part_number="Adafruit #3405"]
  RGB_LED = RGB LED (com. cathode, rgb) [package="5 mm [THT]"]
  R3_(Blue) = Resistor [tolerance=±5% resistance=430 package=THT]
  R2_(Green) = Resistor [tolerance=±5% resistance=430 package=THT]
  R1_(Red) = Resistor [tolerance=±5% resistance=470 package=THT]
  LDR = Photocell (LDR) [package=THT]
  R5_(LED) = Resistor [tolerance=±0.05% resistance=120 package=THT]
  R5_(LDR) = Resistor [tolerance=±0.05% resistance=1k package=THT]
  Switch = Pushbutton [package="[THT]"]
  Yellow_LED = LED - 5mm [color="Yellow (595nm)" package="5 mm [THT]"]

nets:
  N1: Part1.A1_DAC1, Part1.3.3V, LDR.pin_0, LDR.pin_1, Switch.Pin_1, Switch.Pin_2, Switch.Pin_3, Switch.Pin_4
  N2: Part1.A0_DAC2, R5_(LDR).Pin_0
  N3: Part1.GND, RGB_LED.common_cathode, R5_(LED).Pin_1, R5_(LDR).Pin_1
  N4: Part1.IO12_A11, R1_(Red).Pin_0
  N5: Part1.IO27_A10, R3_(Blue).Pin_0
  N6: Part1.IO33_A9, R2_(Green).Pin_0
  N7: Part1.IO14_A6, Yellow_LED.cathode
  N8: RGB_LED.red_anode, R1_(Red).Pin_1
  N9: RGB_LED.green_anode, R2_(Green).Pin_1
  N10: RGB_LED.blue_anode, R3_(Blue).Pin_1
  N11: R5_(LED).Pin_0, Yellow_LED.anode
